# Fritzing sketch Proximity_Sensor_Normal_2 (saved by Fritzing 0.9.4)
breadboards: 1

parts:
  HC-SR04_Sensor_1 = HC-SR04 Ultrasonic Distance Sensor
  LED1 = LED - 5mm [color="Red (633nm)" package="5 mm [THT]"]
  R1 = Resistor [tolerance=±5% resistance=220 package=THT]
  Composant1 = Arduino Uno (Rev3)
  LED2 = LED - 5mm [color="Green (555nm)" package="5 mm [THT]"]
  R2 = Resistor [tolerance=±5% resistance=220 package=THT]

nets:
  VCC: HC-SR04_Sensor_1.VCC, Composant1.5V
  N1: HC-SR04_Sensor_1.TRIG, Composant1.A3
  N2: HC-SR04_Sensor_1.ECHO, Composant1.A2
  GND: HC-SR04_Sensor_1.GND, LED1.cathode, Composant1.GND, LED2.cathode
  N3: LED1.anode, R1.Pin_1
  N4: R1.Pin_0, Composant1.D13/SCK
  N5: Composant1.D12/MISO, R2.Pin_0
  N6: LED2.anode, R2.Pin_1
